# Fritzing sketch Proje (saved by Fritzing 0.9.4)
breadboards: 2

parts:
  Mod1 = Raspberry Pi Pico
  D1 = Rectifier Diode [part_number=1N4001 package="300 mil [THT]"]
  Q1 = NPN-Transistor [package="TO92 [THT]"]
  LED1 = LED - 5mm [color="Red (633nm)" package="5 mm [THT]"]
  LED2 = LED - 5mm [color="Green (570nm)" package="5 mm [THT]"]
  M1 = DC Motor
  LED3 = RGB LED (com. cathode, rgb) [package="5 mm [THT]"]
  R2 = Photocell (LDR) [package=THT]
  T1 = LM35 Temperature Sensor [package="TO92 [THT]"]
  R3 = Resistor [tolerance=±5% resistance=220 package=THT]
  R4 = Resistor [tolerance=±5% resistance=220 package=THT]
  J1 = Piezo Speaker

nets:
  N1: Mod1.pin_1, LED3.red_anode
  N2: Mod1.pin_2, LED3.green_anode
  N3: Mod1.pin_4, LED3.blue_anode
  N4: Mod1.pin_18, Mod1.pin_33, Mod1.pin_38, Mod1.pin_42, Q1.C, LED3.common_cathode, R2.pin_0, T1.GND, R3.Pin_0, R4.Pin_0, J1.pin2
  N5: Mod1.pin_20, J1.pin1
  N6: Mod1.pin_21, Q1.B
  N7: Mod1.pin_22, LED1.anode
  N8: Mod1.pin_24, LED2.anode
  N9: Mod1.pin_31, R2.pin_1
  N10: Mod1.pin_32, T1.Vout
  N11: Mod1.pin_36, T1.+Vs
  N12: Mod1.pin_40, D1.cathode, M1.pin_1
  N13: D1.anode, Q1.E
  N14: LED1.cathode, R3.Pin_1
  N15: LED2.cathode, R4.Pin_1

custom parts:
  Raspberry Pi Pico: Raspberry Pi Pico. Based around the RP2040 microcontroller the Pico is a low cost microcontroller device bringing Raspberry Pi quality, cost, and easy of use to the microcontroller space. Jan 2021, Split part in to two versions: tht (this one) and SMD. This one will drill holes for a .1 in header in pcb to allow plugging in the module as well as providing pads to solder the module to the top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
